# Fritzing sketch worklogPcb01 (saved by Fritzing 0.9.3b)
circuit board: 11.2479cm x 4.71828cm
breadboards: 1

parts:
  MCU1 = Raspberry Pi Zero
  LED1 = LED - 5mm [color="Red (633nm)" package="5 mm [THT]"]
  LED2 = LED - 5mm [color="Red (633nm)" package="5 mm [THT]"]
  LED3 = LED - 5mm [color="Red (633nm)" package="5 mm [THT]"]
  LED4 = LED - 5mm [color="Red (633nm)" package="5 mm [THT]"]
  LED5 = LED - 5mm [color="Red (633nm)" package="5 mm [THT]"]
  LED6 = LED - 5mm [color="Red (633nm)" package="5 mm [THT]"]
  LED7 = LED - 5mm [color="Red (633nm)" package="5 mm [THT]"]
  LED8 = LED - 5mm [color="Red (633nm)" package="5 mm [THT]"]
  LED9 = LED - 5mm [color="Red (633nm)" package="5 mm [THT]"]
  LED10 = LED - 5mm [color="Red (633nm)" package="5 mm [THT]"]
  B1 = Pushbutton [package="[THT]"]
  B2 = Pushbutton [package="[THT]"]
  B3 = Pushbutton [package="[THT]"]
  B4 = Pushbutton [package="[THT]"]
  B5 = Pushbutton [package="[THT]"]
  B6 = Pushbutton [package="[THT]"]
  B7 = Pushbutton [package="[THT]"]
  B8 = Pushbutton [package="[THT]"]
  B9 = Pushbutton [package="[THT]"]
  B10 = Pushbutton [package="[THT]"]
  R1 = Resistor [tolerance=±5% resistance=220 package=THT]
  R2 = Resistor [tolerance=±5% resistance=220 package=THT]
  R3 = Resistor [tolerance=±5% resistance=220 package=THT]
  R4 = Resistor [tolerance=±5% resistance=220 package=THT]
  R5 = Resistor [tolerance=±5% resistance=220 package=THT]
  R6 = Resistor [tolerance=±5% resistance=220 package=THT]
  R7 = Resistor [tolerance=±5% resistance=220 package=THT]
  R8 = Resistor [tolerance=±5% resistance=220 package=THT]
  R9 = Resistor [tolerance=±5% resistance=220 package=THT]
  R10 = Resistor [tolerance=±5% resistance=220 package=THT]

nets:
  N1: MCU1.pin_3, R1.Pin_1
  N2: MCU1.pin_5, R2.Pin_1
  N3: MCU1.pin_6, MCU1.pin_9, MCU1.pin_30, MCU1.pin_39, LED1.cathode, LED2.cathode, LED3.cathode, LED4.cathode, LED5.cathode, LED6.cathode, LED7.cathode, LED8.cathode, LED9.cathode, LED10.cathode, B1.Pin_3, B1.Pin_4, B2.Pin_3, B2.Pin_4, B3.Pin_3, B3.Pin_4, B4.Pin_3, B4.Pin_4, B5.Pin_3, B5.Pin_4, B6.Pin_3, B6.Pin_4, B7.Pin_3, B7.Pin_4, B8.Pin_3, B8.Pin_4, B9.Pin_3, B9.Pin_4, B10.Pin_3, B10.Pin_4
  N4: MCU1.pin_7, R3.Pin_1
  N5: MCU1.pin_11, R4.Pin_1
  N6: MCU1.pin_12, B1.Pin_1, B1.Pin_2
  N7: MCU1.pin_13, R5.Pin_1
  N8: MCU1.pin_15, R6.Pin_1
  N9: MCU1.pin_16, B2.Pin_1, B2.Pin_2
  N10: MCU1.pin_18, B3.Pin_1, B3.Pin_2
  N11: MCU1.pin_19, R7.Pin_1
  N12: MCU1.pin_21, R8.Pin_1
  N13: MCU1.pin_22, B4.Pin_1, B4.Pin_2
  N14: MCU1.pin_23, R9.Pin_1
  N15: MCU1.pin_24, B5.Pin_1, B5.Pin_2
  N16: MCU1.pin_26, B6.Pin_1, B6.Pin_2
  N17: MCU1.pin_28, B7.Pin_1, B7.Pin_2
  N18: MCU1.pin_32, B8.Pin_1, B8.Pin_2
  N19: MCU1.pin_36, B9.Pin_1, B9.Pin_2
  N20: MCU1.pin_37, R10.Pin_1
  N21: MCU1.pin_40, B10.Pin_1, B10.Pin_2
  N22: LED1.anode, R1.Pin_0
  N23: LED2.anode, R2.Pin_0
  N24: LED3.anode, R3.Pin_0
  N25: LED4.anode, R4.Pin_0
  N26: LED5.anode, R5.Pin_0
  N27: LED6.anode, R6.Pin_0
  N28: LED7.anode, R7.Pin_0
  N29: LED8.anode, R8.Pin_0
  N30: LED9.anode, R9.Pin_0
  N31: LED10.anode, R10.Pin_0
